# Fritzing sketch sema (saved by Fritzing 0.8.7b)
breadboards: 1

parts:
  Eleman1 = Arduino Uno (Rev3) - ICSP
  Eleman2 = MQ-4
  U1 = Mystery Part - 2 pins [chip_label=? package=THT]
  Eleman3 = Solar Cell
  Eleman4 = Adafruit USB DC Solar LiPo Charger [part_number="Adafruit #390"]
  U2 = ESP8266 WiFi Module [part_number=ESP8266]
  VCC1 = Battery

nets:
  N1: Eleman1.A0, Eleman2.AO
  N2: Eleman1.ICSP_MOSI, Eleman1.D11_PWM/MOSI, U2.RXD
  N3: Eleman1.D10_PWM/SS, U2.TXD
  VCC: Eleman1.3V3, Eleman2.VCC, U2.VCC, U2.CH_PD
  GND: Eleman1.GND, Eleman2.GND, U1.VOUT-, U2.GND
  N4: Eleman1.VIN, U1.VOUT+
  N5: U1.VIN+, Eleman4.LOAD
  N6: U1.VIN-, Eleman3.-, Eleman4.GND, VCC1.-
  N7: Eleman3.+, Eleman4.DCIN
  N8: Eleman4.BATT, VCC1.+

custom parts:
  Mystery Part - 2 pins: A dummy, proxy, ersatz, stand-in part for whatever you want. With 2 pins on a 100 mil inline pin header footprint.
  Adafruit USB DC Solar LiPo Charger: Make your projects to go green this summer with our specialized USB/Solar Lithium Ion Polymer Battery charger! This charger is a very unique design, perfect for outdoor projects, or DIY iPod chargers. We've spent over a year testing and tinkering with this charger to come up with a plug and play solution to charging batteries with the sun and we're really pleased with what we ended up with.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
  ESP8266 WiFi Module: Generic WiFi Module based on the ESP8266 with onboard PCB antenna and UART communications
  Battery: Your standard 2x 18650 battery pack (7,4 Volts)
